# Fritzing sketch S_W_I_M_S (saved by Fritzing 1.0.2b)

parts:
  Mod1 = Raspberry Pi 4B
  RHT1 = Humidity and Temperature Sensor RHT03
  Part1 = Adafruit ADS1115 16Bit I2C ADC [part_number="Adafruit #1085"]
  Part3 = FC-28 Soil Hygrometer Module - Probe
  Part4 = FC-28 Soil Hygrometer Module
  U1 = Module 4 Relais 5V [package="Module 4 Relais 5V"]
  WATER_PUMP1 = water pump/motor
  USBTTL1 = USB TTL Serial Cable

nets:
  3V3: Mod1.3V3, RHT1.Vcc, Part1.VDD
  VCC: Mod1.5V, Part4.VCC, U1.VCC
  N1: Mod1.GPIO2, Part1.SDA
  N2: Mod1.GPIO3, Part1.SCL
  GND: Mod1.GND, RHT1.GND_2, Part1.GND, Part4.GND, U1.GND, U1.VCC2
  N3: Mod1.GPIO17, RHT1.Data-signal
  N4: Mod1.GPIO27, U1.IN4
  N5: Part1.AIN0, Part4.AO
  N6: Part3.POS, Part4.POS
  N7: Part3.NEG, Part4.NEG
  N8: U1.K4-NF, USBTTL1.5V
  N9: U1.K4-NO, WATER_PUMP1.pin_2
  N10: WATER_PUMP1.pin_1, USBTTL1.GND

notes:
  Hygrometer
  Analog-Digital-Converter
  DHT22:
  Temperature and Humidity
  USB-connection:
  For higher currents
  4-Relais-Module
  Waterpump
  Raspberry Pi

custom parts:
  Adafruit ADS1115 16Bit I2C ADC: For microcontrollers without an analog-to-digital converter or when you want a higher-precision ADC, the ADS1115 provides 16-bit precision at 860 samples/second over I2C. The chip can be configured as 4 single-ended input channels, or two differential channels. As a nice bonus, it even includes a programmable gain amplifier, up to x16, to help boost up smaller single/differential signals to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
  FC-28 Soil Hygrometer Module - Probe: The FC-28 is a soil hygrometer module that uses the Texas Instruments LM393 comparator chip to provide an analog measurement of soil humidity.
  FC-28 Soil Hygrometer Module: The FC-28 is a soil hygrometer module that uses the Texas Instruments LM393 comparator chip to provide an analog measurement of soil humidity. The digital output is high when soil moisture is over a certain threshold, as determined by adjusting the potentiometer.
  Module 4 Relais 5V: Module 4 Relais 5V 4x SPD-06VDC-SD-C
  water pump/motor: WATER PUMP BY ARDUBLOCKTR
